# Fritzing sketch electronic_design (saved by Fritzing 0.9.9b)
breadboards: 1

parts:
  J1 = Basic Servo
  J2 = Basic Servo
  M3 = gear-motor
  Part2 = Motor Driver 1A Dual TB6612FNG
  M4 = gear-motor
  Part3 = Adafruit MAX98357A I2S 3W Class D Amplifier [part_number="Adafruit #3006"]
  HC-SR04_Sensor_1 = HC-SR04 Ultrasonic Distance Sensor
  U1 = LIPO-2000mAh [package=lipo-2000]
  Part6 = Breakout Board for Electret Microphone
  BAT1 = BC9VPC [package=bc9vpc]  # not connected
  M5 = fc-51 [package=THT]
  M6 = fc-51 [package=THT]
  U2 = TCM8240MD [package=tcm8240md]  # not connected
  Jetson_Nano1 = jetsonnano
  Part7 = Arduino Mega 2560 (Rev3)
  U3 = Graphical LCD 128x64 [package=lcd-g12864]  # not connected
  PWM1 = PCA9685 16x12-bit PWM Breakout
  SPKR1 = Loudspeaker

nets:
  N1: J1.pulse, PWM1.no_name_yet#7
  N2: J2.pulse, PWM1.no_name_yet#0
  N3: M3.pin_1, Part2.A02
  N4: M3.pin_2, Part2.A01
  N5: Part2.GND, U1.-, PWM1.no_name_yet#100, PWM1.no_name_yet#107, PWM1.no_name_yet#706
  N6: Part2.B01, M4.pin_1
  N7: Part2.B02, M4.pin_2
  VCC: Part2.VCC, Part3.VIN, HC-SR04_Sensor_1.VCC, Part6.VCC, M5.pin3, M6.pin3, Jetson_Nano1.connector38, PWM1.no_name_yet#605
  GND: Part2.VM, Part3.GND, HC-SR04_Sensor_1.GND, U1.+, Part6.GND, M5.pin2, M6.pin2, Jetson_Nano1.connector37, PWM1.no_name_yet#601, PWM1.no_name_yet#602, PWM1.no_name_yet#701, PWM1.no_name_yet#1000, PWM1.no_name_yet#1007
  N8: Part2.PWMA, Jetson_Nano1.connector15
  N9: Part2.AIN2, Jetson_Nano1.connector21
  N10: Part2.AIN1, Jetson_Nano1.connector17
  N11: Part2.STBY, Jetson_Nano1.connector20
  N12: Part2.BIN1, Jetson_Nano1.connector16
  N13: Part2.BIN2, Jetson_Nano1.connector24
  N14: Part2.PWMB, Jetson_Nano1.connector18
  N15: Part3.DIN, Jetson_Nano1.connector14
  N16: Part3.BCLK, Jetson_Nano1.connector31
  N17: Part3.LRCLK, Jetson_Nano1.connector7
  N18: Part3.VO-, SPKR1.pin1
  N19: Part3.VO+, SPKR1.pin2
  N20: HC-SR04_Sensor_1.TRIG, Jetson_Nano1.connector3
  N21: HC-SR04_Sensor_1.ECHO, Jetson_Nano1.connector5
  N22: Part6.AUD, Jetson_Nano1.connector28
  N23: M5.pin1, Jetson_Nano1.connector6
  N24: M6.pin1, Jetson_Nano1.connector32
  N25: Jetson_Nano1.connector2, Part7.A8
  N26: Jetson_Nano1.connector9, PWM1.no_name_yet#604
  N27: Jetson_Nano1.connector29, PWM1.no_name_yet#603
  N28: Jetson_Nano1.connector35, Part7.A10
  N29: Jetson_Nano1.connector36, Part7.A9

custom parts:
  Adafruit MAX98357A I2S 3W Class D Amplifier: Listen to this good news - we now have an all in one digital audio amp breakout board that works incredibly well with the Raspberry Pi! If you're looking for an easy and low cost way to get you digital sound files bumpin' then the MAX08357 I2S Amp Breakout is for you. It takes standard I2S digital audio input and, not only decodes it into analog, but also amplifies it directly into a speaker.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
